# Fritzing sketch trt (saved by Fritzing 0.9.5d)

parts:
  Bauteil1 = RFID-RC522-v2
  WeMos_D1_Mini1 = WeMos D1 Mini
  Keypad1 = I2C KEYPAD  # not connected
  Bauteil2 = Adafruit I2C+SPI LCD Backpack [part_number="Adafruit #292"]  # not connected

nets:
  N1: Bauteil1.SDA, WeMos_D1_Mini1.D8
  N2: Bauteil1.SCK, WeMos_D1_Mini1.D5
  N3: Bauteil1.MOSI, WeMos_D1_Mini1.D7
  N4: Bauteil1.MISO, WeMos_D1_Mini1.D6
  N5: Bauteil1.IRQ, WeMos_D1_Mini1.D1
  N6: Bauteil1.GND, WeMos_D1_Mini1.G
  N7: Bauteil1.RST, WeMos_D1_Mini1.D3
  3.3V: Bauteil1.3.3V, WeMos_D1_Mini1.3V3

custom parts:
  RFID-RC522-v2: A simple China made RFID-RC522 Reader; do check the pin labels, as this is a MFRC522 based clone.
  I2C KEYPAD: I2C Keypad
  Adafruit I2C+SPI LCD Backpack: LCD backpacks reduce the number of pins needed to connect to an LCD. LCDs are a fun and easy way to have your microcontroller project talk back to you. Character LCDs are common, and easy to get, available in tons of colors and sizes. We've written tutorials on using character LCDs with an Arduino (or similar microcontroller) but find that the number of pins necessary to control the LCD can be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
