# Fritzing sketch trt_v1 (saved by Fritzing 0.9.9b)
circuit board: 11.9263cm x 9.13784cm

parts:
  Bauteil1 = RFID-RC522-v2
  WeMos_D1_Mini1 = WeMos D1 Mini
  ZS-042_RTC1 = ZS-042 RTC Module
  M1 = pcf8574 io expansion board [package=THT]
  LCD2004-I2C1 = LCD2004-I2C
  Keypad4x1 = Keypad Membran 4x4

nets:
  N1: Bauteil1.SDA, WeMos_D1_Mini1.D8
  N2: Bauteil1.SCK, WeMos_D1_Mini1.D5
  N3: Bauteil1.MOSI, WeMos_D1_Mini1.D7
  N4: Bauteil1.MISO, WeMos_D1_Mini1.D6
  N5: Bauteil1.IRQ, WeMos_D1_Mini1.D1
  N6: Bauteil1.GND, WeMos_D1_Mini1.G, ZS-042_RTC1.GND#6
  N7: Bauteil1.RST, WeMos_D1_Mini1.D3
  3.3V: Bauteil1.3.3V, WeMos_D1_Mini1.3V3
  N8: WeMos_D1_Mini1.5V, ZS-042_RTC1.VCC#7
  N9: WeMos_D1_Mini1.D2, ZS-042_RTC1.SDA#8
  N10: WeMos_D1_Mini1.D4, ZS-042_RTC1.SCL#9
  GND: ZS-042_RTC1.GND#0, M1.GND, LCD2004-I2C1.GND
  VCC: ZS-042_RTC1.VCC#1, M1.VCC, LCD2004-I2C1.VCC
  N11: ZS-042_RTC1.SDA#2, M1.SDA, LCD2004-I2C1.SDA
  N12: ZS-042_RTC1.SCL#3, M1.SCL, LCD2004-I2C1.SCL
  N13: M1.O0, Keypad4x1.Pin8
  N14: M1.O1, Keypad4x1.Pin7
  N15: M1.O2, Keypad4x1.Pin6
  N16: M1.O3, Keypad4x1.Pin5
  N17: M1.O4, Keypad4x1.Pin4
  N18: M1.O5, Keypad4x1.Pin3
  N19: M1.O6, Keypad4x1.Pin2
  N20: M1.O7, Keypad4x1.Pin1

custom parts:
  RFID-RC522-v2: A simple China made RFID-RC522 Reader; do check the pin labels, as this is a MFRC522 based clone.
  pcf8574 io expansion board: pcf8574 io expansion board.
  LCD2004-I2C: A standard character display with 4x20 characters. Comes in many colors with LCM2004 IIC attached.
  Keypad Membran 4x4: Membrane Keypad 4x4 Matrix
